# Fritzing sketch PID_Basic (saved by Fritzing 0.9.2b)
breadboards: 1

parts:
  Composant1 = Arduino Nano (Rev3.0)
  R1 = Resistor [tolerance=±5% resistance=220 package=THT]
  C1 = Electrolytic Capacitor [capacitance=1µF package="100 mil [THT, electrolytic]"]
  PWM_gachette = female pin header, 3 pins [form="♀ (female)"]
  S1 = Pushbutton [package=THT]
  S2 = Pushbutton [package=THT]
  S3 = Pushbutton [package=THT]
  VCC_GND_Hall = female pin header, 2 pins [form="♀ (female)"]
  Hall = female pin header, 3 pins [form="♀ (female)"]
  C2 = Ceramic Capacitor [capacitance=100nF package="100 mil [THT, multilayer]"]
  C3 = Ceramic Capacitor [capacitance=100nF package="100 mil [THT, multilayer]"]
  Diode = female pin header, 3 pins [form="♀ (female)"]
  HX711_VCC_GND = female pin header, 2 pins [form="♀ (female)"]
  HX711_Data = female pin header, 2 pins [form="♀ (female)"]

nets:
  GND: Composant1.GND, C1.-, PWM_gachette.pin3, S1.leg1, S2.leg1, S3.leg1, VCC_GND_Hall.pin1, Diode.pin2, HX711_VCC_GND.pin2
  N1: Composant1.D3, S1.leg0
  N2: Composant1.D4, S2.leg0
  N3: Composant1.D5, S3.leg0
  N4: Composant1.D6, R1.Pin_0
  N5: Composant1.D7, HX711_Data.pin2
  N6: Composant1.D8, HX711_Data.pin1
  N7: Composant1.D9, Diode.pin3
  N8: Composant1.VIN, Diode.pin1, HX711_VCC_GND.pin1
  N9: Composant1.A1, Hall.pin2, C2.0
  N10: Composant1.A0, Hall.pin1, C3.0
  N11: R1.Pin_1, C1.+, PWM_gachette.pin2
  N12: VCC_GND_Hall.pin2, C2.1, C3.1
